// Logisim project Lab 1 Solution.circ as structural Verilog: 1 circuit, main circuit main
module main (
  input  A1,
  input  A0,
  input  B1,
  input  B0,
  output X,
  output Y,
  output Z
);

  wire and_1_out, and_2_out, and_3_out, and_4_out, and_5_out, and_6_out, and_7_out, and_8_out, and_9_out,
       and_10_out, not_1_out, not_2_out, not_3_out, not_4_out, or_1_out, or_2_out, or_3_out, or_4_out,
       or_5_out;

  not not_1 (not_1_out, A1);
  not not_2 (not_2_out, A0);
  not not_3 (not_3_out, B1);
  not not_4 (not_4_out, B0);
  and and_1 (and_1_out, not_1_out, B1);
  or or_1 (or_1_out, not_2_out, B0);
  and and_2 (and_2_out, not_3_out, B0);
  and and_3 (and_3_out, A1, A0);
  and and_4 (and_4_out, not_2_out, B1);
  and and_5 (and_5_out, A1, not_3_out);
  or or_2 (or_2_out, and_2_out, and_6_out);
  and and_6 (and_6_out, and_3_out, B0);
  and and_7 (and_7_out, and_4_out, not_4_out);
  or or_3 (or_3_out, and_7_out, and_8_out);
  and and_8 (and_8_out, and_1_out, not_2_out);
  or or_4 (or_4_out, and_1_out, and_9_out);
  and and_9 (and_9_out, and_3_out, not_4_out);
  and and_10 (and_10_out, and_2_out, A0);
  or or_5 (or_5_out, and_10_out, and_5_out);
  and and_11 (X, and_1_out, or_1_out);
  or or_6 (Y, or_2_out, or_3_out);
  or or_7 (Z, or_4_out, or_5_out);
endmodule
